# Fritzing sketch Labirent (saved by Fritzing 0.9.3b)
breadboards: 1

parts:
  Parça1 = Arduino Nano (Rev3.0)
  R1 = Resistor [tolerance=±5% resistance=10k package="2010 [SMD]"]
  S1 = Pushbutton [package="[SMD]"]
  R2 = Resistor [tolerance=±5% resistance=10k package="2010 [SMD]"]
  S2 = Pushbutton [package="[SMD]"]
  R3 = Resistor [tolerance=±5% resistance=10k package="2010 [SMD]"]
  R4 = Resistor [tolerance=±5% resistance=10k package="2010 [SMD]"]
  S3 = Pushbutton [package="[SMD]"]
  S4 = Pushbutton [package="[SMD]"]
  S5 = Pushbutton [package="[SMD]"]
  R5 = Resistor [tolerance=±5% resistance=10k package="2010 [SMD]"]
  J1 = Basic Servo
  J2 = Basic Servo
  VCC1 = Battery

nets:
  N1: Parça1.D3, R1.Pin_0, S1.Pin_1, S1.Pin_2
  N2: Parça1.D4, R2.Pin_0, S2.Pin_1, S2.Pin_2
  N3: Parça1.D5, R3.Pin_0, S3.Pin_1, S3.Pin_2
  N4: Parça1.D6, R4.Pin_0, S4.Pin_1, S4.Pin_2
  N5: Parça1.D7, S5.Pin_1, S5.Pin_2, R5.Pin_0
  N6: Parça1.D9, J2.pulse
  N7: Parça1.D10, J1.pulse
  VCC: Parça1.VIN, S1.Pin_3, S1.Pin_4, S2.Pin_3, S2.Pin_4, S3.Pin_3, S3.Pin_4, S4.Pin_3, S4.Pin_4, S5.Pin_3, S5.Pin_4, J1.vcc, J2.vcc, VCC1.+
  GND: Parça1.GND, R1.Pin_1, R2.Pin_1, R3.Pin_1, R4.Pin_1, R5.Pin_1, J1.gnd, J2.gnd, VCC1.-
